// Logisim project FSM.circ as structural Verilog: 4 circuits, main circuit main
module main (
  input  FSM_Input,
  output FSM_Output
);

  wire clock_1_out;
  wire [1:0] fsmlogic_1_nextstate, register_1_q;

  FSMLogic fsmlogic_1 (
    .Input1(FSM_Input), .CurrentState(register_1_q), .Output1(FSM_Output), .NextState(fsmlogic_1_nextstate));
  Register #(.width(2)) register_1 (.D(fsmlogic_1_nextstate), .clk(clock_1_out), .Q(register_1_q));  // open: en, clr
  Clock clock_1 (.out(clock_1_out));
endmodule

module FSMLogic (
  input  Input1,
  input  [1:0] CurrentState,
  output Output1,
  output [1:0] NextState
);

  StateBitZero statebitzero_1 (.NewState0(NextState[0]));  // open: Input1, StateBit0, StateBit1
  StateBitOne statebitone_1 (.NewState1(NextState[1]));  // open: Input1, StateBit0, StateBit1
endmodule

module StateBitOne (
  input  Input1,
  input  StateBit0,
  input  StateBit1,
  output NewState1
);
endmodule

module StateBitZero (
  input  Input1,
  input  StateBit0,
  input  StateBit1,
  output NewState0
);
endmodule
