// Logisim project FSM_ans.circ as structural Verilog: 4 circuits, main circuit main
module main (
  input  FSM_Input,
  output FSM_Output
);

  wire clock_1_out;
  wire [1:0] fsmlogic_1_next_state, register_1_q;

  FSMLogic fsmlogic_1 (
    .Input(FSM_Input), .Current_State(register_1_q), .Output(FSM_Output), .Next_State(fsmlogic_1_next_state));
  Clock clock_1 (.out(clock_1_out));
  Register #(.width(2)) register_1 (.D(fsmlogic_1_next_state), .Q(register_1_q), .clk(clock_1_out));  // open: en, clr
endmodule

module FSMLogic (
  input  Input,
  input  [1:0] Current_State,
  output Output,
  output [1:0] Next_State
);

  wire and_1_out, and_2_out, not_1_out, not_2_out, not_3_out;

  not not_1 (not_1_out, Input);
  not not_2 (not_2_out, Current_State[0]);
  not not_3 (not_3_out, Current_State[1]);
  and and_1 (and_1_out, Input, not_3_out);
  and and_2 (and_2_out, not_1_out, not_2_out);
  or or_1 (Output, and_1_out, and_2_out);
  StateBitZero statebitzero_1 (
    .Input(Input), .StateBit0(Current_State[0]), .StateBit1(Current_State[1]), .NewState0(Next_State[0]));
  StateBitOne statebitone_1 (
    .Input(Input), .StateBit0(Current_State[0]), .StateBit1(Current_State[1]), .NewState1(Next_State[1]));
endmodule

module StateBitOne (
  input  Input,
  input  StateBit0,
  input  StateBit1,
  output NewState1
);

  or or_1 (NewState1, StateBit1, StateBit0);
endmodule

module StateBitZero (
  input  Input,
  input  StateBit0,
  input  StateBit1,
  output NewState0
);

  wire not_1_out;

  not not_1 (not_1_out, Input);
  or or_1 (NewState0, not_1_out, StateBit1);
endmodule
