// Logisim project ALU.circ as structural Verilog: 2 circuits, main circuit main
module main (
  input  [31:0] in_1
);
endmodule

module ALU (
  input  [31:0] Input1,
  input  [31:0] Input2,
  input  [2:0] in_3,
  output [31:0] out_4
);

  wire [4:0] bit_extender_1_out;
  wire [31:0] AND, OR, shifter_1_out, shifter_2_out, shifter_3_out, shifter_4_out, shifter_5_out, XOR;

  Bit_Extender #(.in_width(32), .out_width(5)) bit_extender_1 (.in(Input2), .out(bit_extender_1_out));
  Shifter #(.width(32)) shifter_1 (.in(Input1), .\dist (bit_extender_1_out), .out(shifter_1_out));
  Shifter #(.width(32), .shift("lr")) shifter_2 (.in(Input1), .\dist (bit_extender_1_out), .out(shifter_2_out));
  Shifter #(.width(32), .shift("ar")) shifter_3 (.in(Input1), .\dist (bit_extender_1_out), .out(shifter_3_out));
  Shifter #(.width(32), .shift("rl")) shifter_4 (.in(Input1), .\dist (bit_extender_1_out), .out(shifter_4_out));
  Shifter #(.width(32), .shift("rr")) shifter_5 (.in(Input1), .\dist (bit_extender_1_out), .out(shifter_5_out));
  assign AND = Input1 & Input2;  // AND_Gate and_1, 32 bits wide
  assign OR = Input1 | Input2;  // OR_Gate or_1, 32 bits wide
  assign XOR = Input1 ^ Input2;  // XOR_Gate xor_1, 32 bits wide
  Multiplexer #(.select(3), .width(32)) multiplexer_1 (
    .in0(shifter_1_out), .in1(shifter_2_out), .in2(shifter_3_out), .in3(shifter_4_out), .in4(shifter_5_out),
    .in5(AND), .in6(OR), .in7(XOR), .out(out_4), .sel(in_3));  // open: en
endmodule
