// Logisim project Shift.circ as structural Verilog: 6 circuits, main circuit main
module main (
  input  [15:0] in_1,
  input  [3:0] in_2,
  output [15:0] out_3
);

  rotr rotr_1 (.in_1(in_1), .in_2(in_2), .out_3(out_3));
endmodule

module _1_bit (
  input  [15:0] in_1,
  output [15:0] out_2
);


  assign out_2 = {in_1[0], in_1[15:1]};
endmodule

module _2_bit (
  input  [15:0] in_1,
  output [15:0] out_2
);


  assign out_2 = {in_1[1:0], in_1[15:2]};
endmodule

module _4_bit (
  input  [15:0] in_1,
  output [15:0] out_2
);


  assign out_2 = {in_1[3:0], in_1[15:4]};
endmodule

module _8_bit (
  input  [15:0] in_1,
  output [15:0] out_2
);


  assign out_2 = {in_1[7:0], in_1[15:8]};
endmodule

module rotr (
  input  [15:0] in_1,
  input  [3:0] in_2,
  output [15:0] out_3
);

  wire [3:0] not_1_out;
  wire [15:0] _1_bit_out_2, _2_bit_out_2, _4_bit_out_2, _8_bit_out_2, multiplexer_1_out, multiplexer_2_out,
       multiplexer_3_out;

  _1_bit _1_bit (.in_1(in_1), .out_2(_1_bit_out_2));
  Multiplexer #(.width(16)) multiplexer_1 (
    .in0(_1_bit_out_2), .in1(in_1), .out(multiplexer_1_out), .sel(not_1_out[0]));  // open: en
  assign not_1_out = ~in_2;  // NOT_Gate not_1, 4 bits wide
  _2_bit _2_bit (.in_1(multiplexer_1_out), .out_2(_2_bit_out_2));
  Multiplexer #(.width(16)) multiplexer_2 (
    .in0(_2_bit_out_2), .in1(multiplexer_1_out), .out(multiplexer_2_out), .sel(not_1_out[1]));  // open: en
  _4_bit _4_bit (.in_1(multiplexer_2_out), .out_2(_4_bit_out_2));
  Multiplexer #(.width(16)) multiplexer_3 (
    .in0(_4_bit_out_2), .in1(multiplexer_2_out), .out(multiplexer_3_out), .sel(not_1_out[2]));  // open: en
  _8_bit _8_bit (.in_1(multiplexer_3_out), .out_2(_8_bit_out_2));
  Multiplexer #(.width(16)) multiplexer_4 (
    .in0(_8_bit_out_2), .in1(multiplexer_3_out), .out(out_3), .sel(not_1_out[3]));  // open: en
endmodule
