// Logisim project fib15.circ as structural Verilog: 1 circuit, main circuit main
module main (
  input  [3:0] in_1,
  output [9:0] out_2
);

  wire clock, comparator_1_eq, stop;
  wire [3:0] counter_1_q;
  wire [9:0] adder_1_out, register_1_q;

  Counter #(.width(4), .max('hf), .ongoal("stay")) counter_1 (
    .Q(counter_1_q), .clk(clock));  // open: load, D, count, carry, clr
  Register #(.width(10)) register_1 (.D(out_2), .en(stop), .Q(register_1_q), .clk(clock));  // open: clr
  Adder #(.width(10)) adder_1 (.a(register_1_q), .b(out_2), .out(adder_1_out));  // open: cin, cout
  not not_1 (stop, comparator_1_eq);
  Comparator #(.width(4), .mode("unsigned")) comparator_1 (
    .a(counter_1_q), .b(in_1), .eq(comparator_1_eq));  // open: gt, lt
  Register #(.width(10)) register_2 (.D(adder_1_out), .en(stop), .Q(out_2), .clk(clock));  // open: clr
  Clock clock_1 (.out(clock));
  // Probe on out_2
endmodule
