// Logisim project alu.circ as structural Verilog
module main (
  input  [5:0] Switch__S,
  input  [31:0] X,
  input  [31:0] Y,
  output Signed_Overflow,
  output [31:0] RESULT,
  output Equal
);

  wire add_Overflow, and_2_out, and_3_out, comparator_2_lt, comparator_3_lt, comparator_4_eq,
       comparator_5_eq, sub_Overflow;
  wire [4:0] bit_extender_1_out, bit_extender_4_out, bit_extender_5_out;
  wire [4:4] _5_bit_instruction;
  wire [31:0] add, addu, \and , bitpal, cnto, \or , sll, slt, sltu, sra, srl, sub, subu;

  xor xor_1 (_5_bit_instruction[4], Switch__S[4], Switch__S[5]);
  Bit_Extender #(.in_width(32), .out_width(5)) bit_extender_1 (.in(Y), .out(bit_extender_1_out));
  Shifter #(.width(32)) shifter_1 (.in(X), .\dist (bit_extender_1_out), .out(sll));
  Comparator #(.width(32)) comparator_1 (.a(X), .b(Y), .eq(Equal));  // open: gt, lt
  Comparator #(.width(32)) comparator_2 (.a(X), .b(Y), .lt(comparator_2_lt));  // open: gt, eq
  assign slt = {{31{1'b0}}, comparator_2_lt};  // Bit_Extender bit_extender_2
  Comparator #(.width(32), .mode("unsigned")) comparator_3 (.a(X), .b(Y), .lt(comparator_3_lt));  // open: gt, eq
  assign sltu = {{31{1'b0}}, comparator_3_lt};  // Bit_Extender bit_extender_3
  Adder #(.width(32)) adder_1 (.a(X), .b(Y), .out(addu));  // open: cin, cout
  add add_1 (.in_1(X), .in_2(Y), .Result(add), .isOverflow(add_Overflow));
  bitpal bitpal_1 (.in_1(X), .out(bitpal));
  Multiplexer #(.select(5), .width(32)) multiplexer_1 (
    .in0(sll), .in2(srl), .in3(sra), .in14(bitpal), .in16(add), .in17(addu), .in18(sub), .in19(subu),
    .in20(\and ), .in21(\or ), .in26(slt), .in27(sltu), .in28(cnto), .out(RESULT),
    .sel({_5_bit_instruction[4], Switch__S[3:0]}));  // open: in1, in4, in5, in6, in7, in8, in9, in10, in11, in12, in13, in15, in22, in23, in24, in25, in29, in30, in31, en
  Bit_Extender #(.in_width(32), .out_width(5)) bit_extender_4 (.in(Y), .out(bit_extender_4_out));
  Bit_Extender #(.in_width(32), .out_width(5)) bit_extender_5 (.in(Y), .out(bit_extender_5_out));
  Shifter #(.width(32), .shift("lr")) shifter_2 (.in(X), .\dist (bit_extender_4_out), .out(srl));
  Shifter #(.width(32), .shift("ar")) shifter_3 (.in(X), .\dist (bit_extender_5_out), .out(sra));
  assign \or  = X | Y;  // OR_Gate or_1, 32 bits wide
  assign \and  = X & Y;  // AND_Gate and_1, 32 bits wide
  Subtractor #(.width(32)) subtractor_1 (.a(X), .b(Y), .out(subu));  // open: bin, bout
  sub sub_1 (.in_1(X), .in_2(Y), .out(sub), .isOverflow(sub_Overflow));
  cnto cnto_1 (.in_1(X), .in_2(Y), .out(cnto));
  Comparator #(.width(6)) comparator_4 (.a(Switch__S), .b(6'b100000), .eq(comparator_4_eq));  // open: gt, lt
  Comparator #(.width(6)) comparator_5 (.a(Switch__S), .b(6'b100010), .eq(comparator_5_eq));  // open: gt, lt
  and and_2 (and_2_out, comparator_4_eq, add_Overflow);
  and and_3 (and_3_out, comparator_5_eq, sub_Overflow);
  or or_2 (Signed_Overflow, and_2_out, and_3_out);

  // Other names for the same wires on the sheet: _5_bit_instruction[3:0] = Switch__S[3:0]; Switch[5:0] = Switch__S;
  //   Eq = Equal; isOver = Signed_Overflow

  // Notes on the sheet:
  //   INPUT to your circuit
  //   INPUTS to your circuit
  //   Divide this switch into 2 parts
  //   First two bits and the rest of bits
  //   First part decides the "set" of instructions
  //   Second part is the # of detailed instruction
  //   DON'T CHANGE THE INPUTS AND OUTPUTS! IF YOU DO SO, YOU NEED TO MAKE SURE THE PINS ARE IN THE RIGHT PLACES!
  //   OUTPUTS of your circuit
endmodule

module add (
  input  [31:0] in_1,
  input  [31:0] in_2,
  output [31:0] Result,
  output isOverflow
);

  wire xor_1_out, xor_2_out;

  Adder #(.width(32)) adder_1 (.a(in_1), .b(in_2), .out(Result));  // open: cin, cout
  xor xor_1 (xor_1_out, in_1[31], Result[31]);
  xor xor_2 (xor_2_out, Result[31], in_2[31]);
  and and_1 (isOverflow, xor_1_out, xor_2_out);
endmodule

module sub (
  input  [31:0] in_1,
  input  [31:0] in_2,
  output [31:0] out,
  output isOverflow
);

  wire xor_1_out, xor_2_out;
  wire [31:0] adder_1_out, not_1_out;

  Subtractor #(.width(32)) subtractor_1 (.a(in_1), .b(in_2), .out(out));  // open: bin, bout
  assign not_1_out = ~in_2;  // NOT_Gate not_1, 32 bits wide
  Adder #(.width(32)) adder_1 (.a(in_1), .b(not_1_out), .out(adder_1_out));  // open: cin, cout
  xor xor_1 (xor_1_out, in_1[31], adder_1_out[31]);
  xor xor_2 (xor_2_out, adder_1_out[31], not_1_out[31]);
  and and_1 (isOverflow, xor_1_out, xor_2_out);
endmodule

module bitpal (
  input  [31:0] in_1,
  output [31:0] out
);

  wire comparator_1_eq;

  Comparator #(.width(16)) comparator_1 (
    .a(in_1[15:0]),
    .b({in_1[16], in_1[17], in_1[18], in_1[19], in_1[20], in_1[21], in_1[22], in_1[23], in_1[24], in_1[25], in_1[26], in_1[27], in_1[28], in_1[29], in_1[30], in_1[31]}),
    .eq(comparator_1_eq));  // open: gt, lt
  assign out = {{31{1'b0}}, comparator_1_eq};  // Bit_Extender bit_extender_1
endmodule

module cnto (
  input  [31:0] in_1,
  input  [31:0] in_2,
  output [31:0] out
);

  wire [31:0] adder_1_out, adder_2_out, adder_3_out, adder_4_out, adder_5_out, adder_6_out, adder_7_out,
       adder_8_out, adder_9_out, adder_10_out, adder_11_out, adder_12_out, adder_13_out, adder_14_out,
       adder_15_out, adder_16_out, adder_17_out, adder_18_out, adder_19_out, adder_20_out, adder_21_out,
       adder_22_out, adder_23_out, adder_24_out, adder_25_out, adder_26_out, adder_27_out, adder_28_out,
       adder_29_out, adder_30_out, adder_31_out, adder_32_out, adder_33_out, adder_34_out, adder_35_out,
       adder_36_out, adder_37_out, adder_38_out, adder_39_out, adder_40_out, adder_41_out, adder_42_out,
       adder_43_out, adder_44_out, adder_45_out, adder_46_out, adder_47_out, adder_48_out, adder_49_out,
       adder_50_out, adder_51_out, adder_52_out, adder_53_out, adder_54_out, adder_55_out, adder_56_out,
       adder_57_out, adder_58_out, adder_59_out, adder_60_out, adder_61_out, adder_62_out,
       bit_extender_1_out, bit_extender_2_out, bit_extender_3_out, bit_extender_4_out, bit_extender_5_out,
       bit_extender_6_out, bit_extender_7_out, bit_extender_8_out, bit_extender_9_out, bit_extender_10_out,
       bit_extender_11_out, bit_extender_12_out, bit_extender_13_out, bit_extender_14_out,
       bit_extender_15_out, bit_extender_16_out, bit_extender_17_out, bit_extender_18_out,
       bit_extender_19_out, bit_extender_20_out, bit_extender_21_out, bit_extender_22_out,
       bit_extender_23_out, bit_extender_24_out, bit_extender_25_out, bit_extender_26_out,
       bit_extender_27_out, bit_extender_28_out, bit_extender_29_out, bit_extender_30_out,
       bit_extender_31_out, bit_extender_32_out, bit_extender_33_out, bit_extender_34_out,
       bit_extender_35_out, bit_extender_36_out, bit_extender_37_out, bit_extender_38_out,
       bit_extender_39_out, bit_extender_40_out, bit_extender_41_out, bit_extender_42_out,
       bit_extender_43_out, bit_extender_44_out, bit_extender_45_out, bit_extender_46_out,
       bit_extender_47_out, bit_extender_48_out, bit_extender_49_out, bit_extender_50_out,
       bit_extender_51_out, bit_extender_52_out, bit_extender_53_out, bit_extender_54_out,
       bit_extender_55_out, bit_extender_56_out, bit_extender_57_out, bit_extender_58_out,
       bit_extender_59_out, bit_extender_60_out, bit_extender_61_out, bit_extender_62_out,
       bit_extender_63_out, bit_extender_64_out;

  assign bit_extender_1_out = {{31{1'b0}}, in_1[0]};  // Bit_Extender bit_extender_1
  assign bit_extender_2_out = {{31{1'b0}}, in_1[1]};  // Bit_Extender bit_extender_2
  assign bit_extender_3_out = {{31{1'b0}}, in_1[2]};  // Bit_Extender bit_extender_3
  assign bit_extender_4_out = {{31{1'b0}}, in_1[3]};  // Bit_Extender bit_extender_4
  assign bit_extender_5_out = {{31{1'b0}}, in_1[4]};  // Bit_Extender bit_extender_5
  assign bit_extender_6_out = {{31{1'b0}}, in_1[5]};  // Bit_Extender bit_extender_6
  assign bit_extender_7_out = {{31{1'b0}}, in_1[6]};  // Bit_Extender bit_extender_7
  assign bit_extender_8_out = {{31{1'b0}}, in_1[7]};  // Bit_Extender bit_extender_8
  assign bit_extender_9_out = {{31{1'b0}}, in_1[8]};  // Bit_Extender bit_extender_9
  assign bit_extender_10_out = {{31{1'b0}}, in_1[9]};  // Bit_Extender bit_extender_10
  assign bit_extender_11_out = {{31{1'b0}}, in_1[10]};  // Bit_Extender bit_extender_11
  assign bit_extender_12_out = {{31{1'b0}}, in_1[11]};  // Bit_Extender bit_extender_12
  assign bit_extender_13_out = {{31{1'b0}}, in_1[12]};  // Bit_Extender bit_extender_13
  assign bit_extender_14_out = {{31{1'b0}}, in_1[13]};  // Bit_Extender bit_extender_14
  assign bit_extender_15_out = {{31{1'b0}}, in_1[14]};  // Bit_Extender bit_extender_15
  assign bit_extender_16_out = {{31{1'b0}}, in_1[15]};  // Bit_Extender bit_extender_16
  assign bit_extender_17_out = {{31{1'b0}}, in_1[16]};  // Bit_Extender bit_extender_17
  assign bit_extender_18_out = {{31{1'b0}}, in_1[17]};  // Bit_Extender bit_extender_18
  assign bit_extender_19_out = {{31{1'b0}}, in_1[18]};  // Bit_Extender bit_extender_19
  assign bit_extender_20_out = {{31{1'b0}}, in_1[19]};  // Bit_Extender bit_extender_20
  assign bit_extender_21_out = {{31{1'b0}}, in_1[20]};  // Bit_Extender bit_extender_21
  assign bit_extender_22_out = {{31{1'b0}}, in_1[21]};  // Bit_Extender bit_extender_22
  assign bit_extender_23_out = {{31{1'b0}}, in_1[22]};  // Bit_Extender bit_extender_23
  assign bit_extender_24_out = {{31{1'b0}}, in_1[23]};  // Bit_Extender bit_extender_24
  assign bit_extender_25_out = {{31{1'b0}}, in_1[24]};  // Bit_Extender bit_extender_25
  assign bit_extender_26_out = {{31{1'b0}}, in_1[25]};  // Bit_Extender bit_extender_26
  assign bit_extender_27_out = {{31{1'b0}}, in_1[26]};  // Bit_Extender bit_extender_27
  assign bit_extender_28_out = {{31{1'b0}}, in_1[27]};  // Bit_Extender bit_extender_28
  assign bit_extender_29_out = {{31{1'b0}}, in_1[28]};  // Bit_Extender bit_extender_29
  assign bit_extender_30_out = {{31{1'b0}}, in_1[29]};  // Bit_Extender bit_extender_30
  assign bit_extender_31_out = {{31{1'b0}}, in_1[30]};  // Bit_Extender bit_extender_31
  assign bit_extender_32_out = {{31{1'b0}}, in_1[31]};  // Bit_Extender bit_extender_32
  assign bit_extender_33_out = {{31{1'b0}}, in_2[0]};  // Bit_Extender bit_extender_33
  assign bit_extender_34_out = {{31{1'b0}}, in_2[1]};  // Bit_Extender bit_extender_34
  assign bit_extender_35_out = {{31{1'b0}}, in_2[2]};  // Bit_Extender bit_extender_35
  assign bit_extender_36_out = {{31{1'b0}}, in_2[3]};  // Bit_Extender bit_extender_36
  assign bit_extender_37_out = {{31{1'b0}}, in_2[4]};  // Bit_Extender bit_extender_37
  assign bit_extender_38_out = {{31{1'b0}}, in_2[5]};  // Bit_Extender bit_extender_38
  assign bit_extender_39_out = {{31{1'b0}}, in_2[6]};  // Bit_Extender bit_extender_39
  assign bit_extender_40_out = {{31{1'b0}}, in_2[7]};  // Bit_Extender bit_extender_40
  assign bit_extender_41_out = {{31{1'b0}}, in_2[8]};  // Bit_Extender bit_extender_41
  assign bit_extender_42_out = {{31{1'b0}}, in_2[9]};  // Bit_Extender bit_extender_42
  assign bit_extender_43_out = {{31{1'b0}}, in_2[10]};  // Bit_Extender bit_extender_43
  assign bit_extender_44_out = {{31{1'b0}}, in_2[11]};  // Bit_Extender bit_extender_44
  assign bit_extender_45_out = {{31{1'b0}}, in_2[12]};  // Bit_Extender bit_extender_45
  assign bit_extender_46_out = {{31{1'b0}}, in_2[13]};  // Bit_Extender bit_extender_46
  assign bit_extender_47_out = {{31{1'b0}}, in_2[14]};  // Bit_Extender bit_extender_47
  assign bit_extender_48_out = {{31{1'b0}}, in_2[15]};  // Bit_Extender bit_extender_48
  assign bit_extender_49_out = {{31{1'b0}}, in_2[16]};  // Bit_Extender bit_extender_49
  assign bit_extender_50_out = {{31{1'b0}}, in_2[17]};  // Bit_Extender bit_extender_50
  assign bit_extender_51_out = {{31{1'b0}}, in_2[18]};  // Bit_Extender bit_extender_51
  assign bit_extender_52_out = {{31{1'b0}}, in_2[19]};  // Bit_Extender bit_extender_52
  assign bit_extender_53_out = {{31{1'b0}}, in_2[20]};  // Bit_Extender bit_extender_53
  assign bit_extender_54_out = {{31{1'b0}}, in_2[21]};  // Bit_Extender bit_extender_54
  assign bit_extender_55_out = {{31{1'b0}}, in_2[22]};  // Bit_Extender bit_extender_55
  assign bit_extender_56_out = {{31{1'b0}}, in_2[23]};  // Bit_Extender bit_extender_56
  assign bit_extender_57_out = {{31{1'b0}}, in_2[24]};  // Bit_Extender bit_extender_57
  assign bit_extender_58_out = {{31{1'b0}}, in_2[25]};  // Bit_Extender bit_extender_58
  assign bit_extender_59_out = {{31{1'b0}}, in_2[26]};  // Bit_Extender bit_extender_59
  assign bit_extender_60_out = {{31{1'b0}}, in_2[27]};  // Bit_Extender bit_extender_60
  assign bit_extender_61_out = {{31{1'b0}}, in_2[28]};  // Bit_Extender bit_extender_61
  assign bit_extender_62_out = {{31{1'b0}}, in_2[29]};  // Bit_Extender bit_extender_62
  assign bit_extender_63_out = {{31{1'b0}}, in_2[30]};  // Bit_Extender bit_extender_63
  assign bit_extender_64_out = {{31{1'b0}}, in_2[31]};  // Bit_Extender bit_extender_64
  Adder #(.width(32)) adder_1 (.a(bit_extender_1_out), .b(bit_extender_2_out), .out(adder_1_out));  // open: cin, cout
  Adder #(.width(32)) adder_2 (.a(adder_1_out), .b(bit_extender_3_out), .out(adder_2_out));  // open: cin, cout
  Adder #(.width(32)) adder_3 (.a(bit_extender_33_out), .b(bit_extender_34_out), .out(adder_3_out));  // open: cin, cout
  Adder #(.width(32)) adder_4 (.a(adder_3_out), .b(bit_extender_35_out), .out(adder_4_out));  // open: cin, cout
  Adder #(.width(32)) adder_5 (.a(adder_2_out), .b(bit_extender_4_out), .out(adder_5_out));  // open: cin, cout
  Adder #(.width(32)) adder_6 (.a(adder_4_out), .b(bit_extender_36_out), .out(adder_6_out));  // open: cin, cout
  Adder #(.width(32)) adder_7 (.a(adder_5_out), .b(bit_extender_5_out), .out(adder_7_out));  // open: cin, cout
  Adder #(.width(32)) adder_8 (.a(adder_6_out), .b(bit_extender_37_out), .out(adder_8_out));  // open: cin, cout
  Adder #(.width(32)) adder_9 (.a(adder_7_out), .b(bit_extender_6_out), .out(adder_9_out));  // open: cin, cout
  Adder #(.width(32)) adder_10 (.a(adder_9_out), .b(bit_extender_7_out), .out(adder_10_out));  // open: cin, cout
  Adder #(.width(32)) adder_11 (.a(adder_8_out), .b(bit_extender_38_out), .out(adder_11_out));  // open: cin, cout
  Adder #(.width(32)) adder_12 (.a(adder_11_out), .b(bit_extender_39_out), .out(adder_12_out));  // open: cin, cout
  Adder #(.width(32)) adder_13 (.a(adder_10_out), .b(bit_extender_8_out), .out(adder_13_out));  // open: cin, cout
  Adder #(.width(32)) adder_14 (.a(adder_12_out), .b(bit_extender_40_out), .out(adder_14_out));  // open: cin, cout
  Adder #(.width(32)) adder_15 (.a(adder_13_out), .b(bit_extender_9_out), .out(adder_15_out));  // open: cin, cout
  Adder #(.width(32)) adder_16 (.a(adder_14_out), .b(bit_extender_41_out), .out(adder_16_out));  // open: cin, cout
  Adder #(.width(32)) adder_17 (.a(adder_15_out), .b(bit_extender_10_out), .out(adder_17_out));  // open: cin, cout
  Adder #(.width(32)) adder_18 (.a(adder_17_out), .b(bit_extender_11_out), .out(adder_18_out));  // open: cin, cout
  Adder #(.width(32)) adder_19 (.a(adder_16_out), .b(bit_extender_42_out), .out(adder_19_out));  // open: cin, cout
  Adder #(.width(32)) adder_20 (.a(adder_19_out), .b(bit_extender_43_out), .out(adder_20_out));  // open: cin, cout
  Adder #(.width(32)) adder_21 (.a(adder_18_out), .b(bit_extender_12_out), .out(adder_21_out));  // open: cin, cout
  Adder #(.width(32)) adder_22 (.a(adder_20_out), .b(bit_extender_44_out), .out(adder_22_out));  // open: cin, cout
  Adder #(.width(32)) adder_23 (.a(adder_21_out), .b(bit_extender_13_out), .out(adder_23_out));  // open: cin, cout
  Adder #(.width(32)) adder_24 (.a(adder_22_out), .b(bit_extender_45_out), .out(adder_24_out));  // open: cin, cout
  Adder #(.width(32)) adder_25 (.a(adder_23_out), .b(bit_extender_14_out), .out(adder_25_out));  // open: cin, cout
  Adder #(.width(32)) adder_26 (.a(adder_25_out), .b(bit_extender_15_out), .out(adder_26_out));  // open: cin, cout
  Adder #(.width(32)) adder_27 (.a(adder_24_out), .b(bit_extender_46_out), .out(adder_27_out));  // open: cin, cout
  Adder #(.width(32)) adder_28 (.a(adder_27_out), .b(bit_extender_47_out), .out(adder_28_out));  // open: cin, cout
  Adder #(.width(32)) adder_29 (.a(adder_26_out), .b(bit_extender_16_out), .out(adder_29_out));  // open: cin, cout
  Adder #(.width(32)) adder_30 (.a(adder_28_out), .b(bit_extender_48_out), .out(adder_30_out));  // open: cin, cout
  Adder #(.width(32)) adder_31 (.a(adder_29_out), .b(bit_extender_17_out), .out(adder_31_out));  // open: cin, cout
  Adder #(.width(32)) adder_32 (.a(adder_30_out), .b(bit_extender_49_out), .out(adder_32_out));  // open: cin, cout
  Adder #(.width(32)) adder_33 (.a(adder_31_out), .b(bit_extender_18_out), .out(adder_33_out));  // open: cin, cout
  Adder #(.width(32)) adder_34 (.a(adder_33_out), .b(bit_extender_19_out), .out(adder_34_out));  // open: cin, cout
  Adder #(.width(32)) adder_35 (.a(adder_32_out), .b(bit_extender_50_out), .out(adder_35_out));  // open: cin, cout
  Adder #(.width(32)) adder_36 (.a(adder_35_out), .b(bit_extender_51_out), .out(adder_36_out));  // open: cin, cout
  Adder #(.width(32)) adder_37 (.a(adder_34_out), .b(bit_extender_20_out), .out(adder_37_out));  // open: cin, cout
  Adder #(.width(32)) adder_38 (.a(adder_36_out), .b(bit_extender_52_out), .out(adder_38_out));  // open: cin, cout
  Adder #(.width(32)) adder_39 (.a(adder_37_out), .b(bit_extender_21_out), .out(adder_39_out));  // open: cin, cout
  Adder #(.width(32)) adder_40 (.a(adder_38_out), .b(bit_extender_53_out), .out(adder_40_out));  // open: cin, cout
  Adder #(.width(32)) adder_41 (.a(adder_39_out), .b(bit_extender_22_out), .out(adder_41_out));  // open: cin, cout
  Adder #(.width(32)) adder_42 (.a(adder_41_out), .b(bit_extender_23_out), .out(adder_42_out));  // open: cin, cout
  Adder #(.width(32)) adder_43 (.a(adder_40_out), .b(bit_extender_54_out), .out(adder_43_out));  // open: cin, cout
  Adder #(.width(32)) adder_44 (.a(adder_43_out), .b(bit_extender_55_out), .out(adder_44_out));  // open: cin, cout
  Adder #(.width(32)) adder_45 (.a(adder_42_out), .b(bit_extender_24_out), .out(adder_45_out));  // open: cin, cout
  Adder #(.width(32)) adder_46 (.a(adder_44_out), .b(bit_extender_56_out), .out(adder_46_out));  // open: cin, cout
  Adder #(.width(32)) adder_47 (.a(adder_45_out), .b(bit_extender_25_out), .out(adder_47_out));  // open: cin, cout
  Adder #(.width(32)) adder_48 (.a(adder_46_out), .b(bit_extender_57_out), .out(adder_48_out));  // open: cin, cout
  Adder #(.width(32)) adder_49 (.a(adder_47_out), .b(bit_extender_26_out), .out(adder_49_out));  // open: cin, cout
  Adder #(.width(32)) adder_50 (.a(adder_49_out), .b(bit_extender_27_out), .out(adder_50_out));  // open: cin, cout
  Adder #(.width(32)) adder_51 (.a(adder_48_out), .b(bit_extender_58_out), .out(adder_51_out));  // open: cin, cout
  Adder #(.width(32)) adder_52 (.a(adder_51_out), .b(bit_extender_59_out), .out(adder_52_out));  // open: cin, cout
  Adder #(.width(32)) adder_53 (.a(adder_50_out), .b(bit_extender_28_out), .out(adder_53_out));  // open: cin, cout
  Adder #(.width(32)) adder_54 (.a(adder_52_out), .b(bit_extender_60_out), .out(adder_54_out));  // open: cin, cout
  Adder #(.width(32)) adder_55 (.a(adder_53_out), .b(bit_extender_29_out), .out(adder_55_out));  // open: cin, cout
  Adder #(.width(32)) adder_56 (.a(adder_54_out), .b(bit_extender_61_out), .out(adder_56_out));  // open: cin, cout
  Adder #(.width(32)) adder_57 (.a(adder_55_out), .b(bit_extender_30_out), .out(adder_57_out));  // open: cin, cout
  Adder #(.width(32)) adder_58 (.a(adder_57_out), .b(bit_extender_31_out), .out(adder_58_out));  // open: cin, cout
  Adder #(.width(32)) adder_59 (.a(adder_56_out), .b(bit_extender_62_out), .out(adder_59_out));  // open: cin, cout
  Adder #(.width(32)) adder_60 (.a(adder_59_out), .b(bit_extender_63_out), .out(adder_60_out));  // open: cin, cout
  Adder #(.width(32)) adder_61 (.a(adder_58_out), .b(bit_extender_32_out), .out(adder_61_out));  // open: cin, cout
  Adder #(.width(32)) adder_62 (.a(adder_60_out), .b(bit_extender_64_out), .out(adder_62_out));  // open: cin, cout
  Adder #(.width(32)) adder_63 (.a(adder_61_out), .b(adder_62_out), .out(out));  // open: cin, cout
endmodule
